// Logisim project Group_Project.circ as structural Verilog: 19 circuits, main circuit TrafficLightBrain
module Main (
  input  E,
  input  X,
  input  in_3
);

  wire clock_1_out, leselector_1_green, leselector_1_red, leselector_1_yellow, lxselector_1_green,
       lxselector_1_red, lxselector_1_yellow, seg7_1_out_5, seg7_1_out_6, seg7_1_out_7, seg7_1_out_8,
       seg7_1_out_9, seg7_1_out_10, seg7_1_out_11, trafficlightbrain_1_c00, trafficlightbrain_1_c11,
       trafficlightbrain_1_c22, trafficlightbrain_1_c33, trafficlightbrain_1_le00, trafficlightbrain_1_le11,
       trafficlightbrain_1_lx00, trafficlightbrain_1_lx11;

  Clock clock_1 (.out(clock_1_out));
  TrafficLightBrain trafficlightbrain_1 (
    .E(E), .X(X), .in_3(clock_1_out), .R(in_3), .LE00(trafficlightbrain_1_le00),
    .LE11(trafficlightbrain_1_le11), .LX00(trafficlightbrain_1_lx00), .LX11(trafficlightbrain_1_lx11),
    .C33(trafficlightbrain_1_c33), .C22(trafficlightbrain_1_c22), .C11(trafficlightbrain_1_c11),
    .C00(trafficlightbrain_1_c00));
  LED led_1 (.in(lxselector_1_red));
  LXSelector lxselector_1 (
    .Lx1(trafficlightbrain_1_lx11), .Lx0(trafficlightbrain_1_lx00), .Red(lxselector_1_red),
    .Yellow(lxselector_1_yellow), .Green(lxselector_1_green));
  LED led_2 (.in(lxselector_1_yellow));
  LED led_3 (.in(lxselector_1_green));
  LESelector leselector_1 (
    .Le1(trafficlightbrain_1_le11), .Le0(trafficlightbrain_1_le00), .Red(leselector_1_red),
    .Yellow(leselector_1_yellow), .Green(leselector_1_green));
  Seg7 seg7_1 (
    .in_1(trafficlightbrain_1_c00), .in_2(trafficlightbrain_1_c11), .in_3(trafficlightbrain_1_c22),
    .in_4(trafficlightbrain_1_c33), .out_5(seg7_1_out_5), .out_6(seg7_1_out_6), .out_7(seg7_1_out_7),
    .out_8(seg7_1_out_8), .out_9(seg7_1_out_9), .out_10(seg7_1_out_10), .out_11(seg7_1_out_11));
  LED led_4 (.in(leselector_1_red));
  LED led_5 (.in(leselector_1_yellow));
  LED led_6 (.in(leselector_1_green));
  _7_Segment_Display u_7_segment_display_1 (
    .g(seg7_1_out_11), .f(seg7_1_out_10), .a(seg7_1_out_5), .b(seg7_1_out_6), .e(seg7_1_out_9),
    .d(seg7_1_out_8), .c(seg7_1_out_7));  // open: dp
endmodule

module TrafficLightBrain (
  input  E,
  input  X,
  input  in_3,
  input  R,
  output LE00,
  output LE11,
  output LX00,
  output LX11,
  output C33,
  output C22,
  output C11,
  output C00
);

  wire [5:0] b0prime_1_o, register_1_q;

  B0Prime b0prime_1 (
    .B5(register_1_q[5]), .B4(register_1_q[4]), .B3(register_1_q[3]), .B2(register_1_q[2]),
    .B1(register_1_q[1]), .B0(register_1_q[0]), .E(E), .X(X), .O(b0prime_1_o[0]));
  B1Prime b1prime_1 (
    .B5(register_1_q[5]), .B4(register_1_q[4]), .B3(register_1_q[3]), .B2(register_1_q[2]),
    .B1(register_1_q[1]), .B0(register_1_q[0]), .E(E), .X(X), .O(b0prime_1_o[1]));
  B2Prime b2prime_1 (
    .B5(register_1_q[5]), .B4(register_1_q[4]), .B3(register_1_q[3]), .B2(register_1_q[2]),
    .B1(register_1_q[1]), .B0(register_1_q[0]), .E(E), .X(X), .O(b0prime_1_o[2]));
  B3Prime b3prime_1 (
    .B5(register_1_q[5]), .B4(register_1_q[4]), .B3(register_1_q[3]), .B2(register_1_q[2]),
    .B1(register_1_q[1]), .B0(register_1_q[0]), .E(E), .X(X), .O(b0prime_1_o[3]));
  B4Prime b4prime_1 (
    .B5(register_1_q[5]), .B4(register_1_q[4]), .B3(register_1_q[3]), .B2(register_1_q[2]),
    .B1(register_1_q[1]), .B0(register_1_q[0]), .E(E), .X(X), .O(b0prime_1_o[4]));
  B5Prime b5prime_1 (
    .B5(register_1_q[5]), .B4(register_1_q[4]), .B3(register_1_q[3]), .B2(register_1_q[2]),
    .B1(register_1_q[1]), .B0(register_1_q[0]), .E(E), .X(X), .O(b0prime_1_o[5]));
  Register #(.width(6)) register_1 (.D(b0prime_1_o), .clk(in_3), .Q(register_1_q), .clr(R));  // open: en
  LE0 le0_1 (
    .B5(register_1_q[5]), .B4(register_1_q[4]), .B3(register_1_q[3]), .B2(register_1_q[2]),
    .B1(register_1_q[1]), .B0(register_1_q[0]), .O(LE00));
  LE1 le1_1 (
    .B5(register_1_q[5]), .B4(register_1_q[4]), .B3(register_1_q[3]), .B2(register_1_q[2]),
    .B1(register_1_q[1]), .B0(register_1_q[0]), .O(LE11));
  LX0 lx0_1 (
    .B5(register_1_q[5]), .B4(register_1_q[4]), .B3(register_1_q[3]), .B2(register_1_q[2]),
    .B1(register_1_q[1]), .B0(register_1_q[0]), .O(LX00));
  LX1 lx1_1 (
    .B5(register_1_q[5]), .B4(register_1_q[4]), .B3(register_1_q[3]), .B2(register_1_q[2]),
    .B1(register_1_q[1]), .B0(register_1_q[0]), .O(LX11));
  C3 c3_1 (
    .B5(register_1_q[5]), .B4(register_1_q[4]), .B3(register_1_q[3]), .B2(register_1_q[2]),
    .B1(register_1_q[1]), .B0(register_1_q[0]), .O(C33));
  C2 c2_1 (
    .B5(register_1_q[5]), .B4(register_1_q[4]), .B3(register_1_q[3]), .B2(register_1_q[2]),
    .B1(register_1_q[1]), .B0(register_1_q[0]), .O(C22));
  C1 c1_1 (
    .B5(register_1_q[5]), .B4(register_1_q[4]), .B3(register_1_q[3]), .B2(register_1_q[2]),
    .B1(register_1_q[1]), .B0(register_1_q[0]), .O(C11));
  C0 c0_1 (
    .B5(register_1_q[5]), .B4(register_1_q[4]), .B3(register_1_q[3]), .B2(register_1_q[2]),
    .B1(register_1_q[1]), .B0(register_1_q[0]), .O(C00));
endmodule

module LE1 (
  input  B5,
  input  B4,
  input  B3,
  input  B2,
  input  B1,
  input  B0,
  output O
);

  wire and_1_out, and_2_out, and_3_out, and_4_out, not_1_out, not_2_out, not_3_out, not_4_out, not_5_out;

  not not_1 (not_1_out, B5);
  not not_2 (not_2_out, B4);
  not not_3 (not_3_out, B2);
  not not_4 (not_4_out, B1);
  not not_5 (not_5_out, B0);
  and and_1 (and_1_out, not_1_out, not_2_out, B3, not_3_out, B1, not_5_out);
  and and_2 (and_2_out, B3, B2, not_4_out);
  and and_3 (and_3_out, B4, not_4_out);
  and and_4 (and_4_out, B5, not_4_out);
  or or_1 (O, and_1_out, and_2_out, and_3_out, and_4_out);
endmodule

module LE0 (
  input  B5,
  input  B4,
  input  B3,
  input  B2,
  input  B1,
  input  B0,
  output O
);

  wire and_1_out, and_2_out, and_3_out;

  and and_1 (and_1_out, B3, B1, B0);
  and and_2 (and_2_out, B4, B1, B0);
  and and_3 (and_3_out, B5, B1, B0);
  or or_1 (O, and_1_out, and_2_out, and_3_out);
endmodule

module LX1 (
  input  B5,
  input  B4,
  input  B3,
  input  B2,
  input  B1,
  input  B0,
  output O
);

  wire and_1_out, and_2_out, and_3_out, and_4_out, and_5_out, and_6_out, and_7_out, not_1_out, not_2_out,
       not_3_out, not_4_out, not_5_out;

  not not_1 (not_1_out, B5);
  not not_2 (not_2_out, B4);
  not not_3 (not_3_out, B3);
  not not_4 (not_4_out, B2);
  not not_5 (not_5_out, B1);
  and and_1 (and_1_out, not_1_out, not_2_out, not_3_out);
  and and_2 (and_2_out, not_1_out, not_2_out, not_4_out, not_5_out);
  and and_3 (and_3_out, not_1_out, not_2_out, not_4_out, B0);
  and and_4 (and_4_out, B1, B0);
  and and_5 (and_5_out, B2, B1);
  and and_6 (and_6_out, B4, B1);
  and and_7 (and_7_out, B5, B1);
  or or_1 (O, and_1_out, and_2_out, and_3_out, and_4_out, and_5_out, and_6_out, and_7_out);
endmodule

module LX0 (
  input  B5,
  input  B4,
  input  B3,
  input  B2,
  input  B1,
  input  B0,
  output O
);

  wire and_1_out, and_2_out, and_3_out, and_4_out, not_1_out, not_2_out, not_3_out, not_4_out, not_5_out;

  not not_1 (not_1_out, B5);
  not not_2 (not_2_out, B4);
  not not_3 (not_3_out, B2);
  not not_4 (not_4_out, B1);
  not not_5 (not_5_out, B0);
  and and_1 (and_1_out, not_1_out, not_2_out, B3, not_3_out, B1, not_5_out);
  and and_2 (and_2_out, B3, B2, not_4_out, B0);
  and and_3 (and_3_out, B4, not_4_out, B0);
  and and_4 (and_4_out, B5, not_4_out, B0);
  or or_1 (O, and_1_out, and_2_out, and_3_out, and_4_out);
endmodule

module B5Prime (
  input  B5,
  input  B4,
  input  B3,
  input  B2,
  input  B1,
  input  B0,
  input  E,
  input  X,
  output O
);

  wire and_1_out, and_2_out, and_3_out, and_4_out, and_5_out, and_6_out, not_1_out, not_2_out, not_3_out,
       not_4_out, not_5_out;

  not not_1 (not_1_out, B4);
  not not_2 (not_2_out, B3);
  not not_3 (not_3_out, B2);
  not not_4 (not_4_out, B1);
  not not_5 (not_5_out, X);
  and and_1 (and_1_out, not_1_out, not_2_out, B2, B1, B0, X);
  and and_2 (and_2_out, not_1_out, B3, not_3_out, not_4_out, X);
  and and_3 (and_3_out, B4, B3, B2, B1, B0);
  and and_4 (and_4_out, B5, not_4_out, not_5_out);
  and and_5 (and_5_out, B5, B0);
  and and_6 (and_6_out, B5, B2, not_4_out);
  or or_1 (O, and_1_out, and_2_out, and_3_out, and_4_out, and_5_out, and_6_out);
endmodule

module B4Prime (
  input  B5,
  input  B4,
  input  B3,
  input  B2,
  input  B1,
  input  B0,
  input  E,
  input  X,
  output O
);

  wire and_1_out, and_2_out, and_3_out, and_4_out, and_5_out, and_6_out, and_7_out, and_8_out, and_9_out,
       not_1_out, not_2_out, not_3_out, not_4_out, not_5_out, not_6_out, not_7_out;

  not not_1 (not_1_out, B5);
  not not_2 (not_2_out, B4);
  not not_3 (not_3_out, B3);
  not not_4 (not_4_out, B2);
  not not_5 (not_5_out, B1);
  not not_6 (not_6_out, B0);
  not not_7 (not_7_out, X);
  and and_1 (and_1_out, not_1_out, not_3_out, not_4_out, B1, B0, X);
  and and_2 (and_2_out, not_1_out, not_2_out, not_3_out, B2, not_6_out, X);
  and and_3 (and_3_out, not_1_out, not_3_out, B2, not_5_out, X);
  and and_4 (and_4_out, not_2_out, B3, B2, B1, B0);
  and and_5 (and_5_out, B4, not_5_out, not_7_out);
  and and_6 (and_6_out, B4, not_3_out, B0);
  and and_7 (and_7_out, B4, not_4_out, B0);
  and and_8 (and_8_out, B4, B3, not_5_out);
  and and_9 (and_9_out, B5, not_3_out, not_4_out, not_5_out, not_6_out, X);
  or or_1 (O, and_1_out, and_2_out, and_3_out, and_4_out, and_5_out, and_6_out, and_7_out, and_8_out, and_9_out);
endmodule

module B3Prime (
  input  B5,
  input  B4,
  input  B3,
  input  B2,
  input  B1,
  input  B0,
  input  E,
  input  X,
  output O
);

  wire and_1_out, and_2_out, and_3_out, and_4_out, and_5_out, and_6_out, and_7_out, and_8_out, and_9_out,
       and_10_out, and_11_out, and_12_out, and_13_out, not_1_out, not_2_out, not_3_out, not_4_out, not_5_out,
       not_6_out, not_7_out;

  not not_1 (not_1_out, B5);
  not not_2 (not_2_out, B4);
  not not_3 (not_3_out, B3);
  not not_4 (not_4_out, B2);
  not not_5 (not_5_out, B1);
  not not_6 (not_6_out, B0);
  not not_7 (not_7_out, X);
  and and_1 (and_1_out, not_1_out, not_2_out, not_5_out, B0, X);
  and and_2 (and_2_out, not_1_out, not_2_out, not_3_out, B1, not_6_out, X);
  and and_3 (and_3_out, not_3_out, B2, B1, B0, E, not_7_out);
  and and_4 (and_4_out, B3, not_5_out, not_7_out);
  and and_5 (and_5_out, B3, not_4_out, B0);
  and and_6 (and_6_out, B3, B2, not_5_out);
  and and_7 (and_7_out, B4, not_3_out, not_4_out, not_5_out, not_6_out, X);
  and and_8 (and_8_out, B4, not_3_out, B2, B1, B0);
  and and_9 (and_9_out, B5, not_3_out, not_4_out, not_5_out, not_6_out, X);
  and and_10 (and_10_out, B5, B2, B1, E);
  and and_11 (and_11_out, B5, B2, B1, B0);
  and and_12 (and_12_out, B5, B3, B0);
  and and_13 (and_13_out, B5, B3, B1);
  or or_1 (O, and_1_out, and_2_out, and_3_out, and_4_out, and_5_out, and_6_out, and_7_out, and_8_out, and_9_out, and_10_out, and_11_out, and_12_out, and_13_out);
endmodule

module B2Prime (
  input  B5,
  input  B4,
  input  B3,
  input  B2,
  input  B1,
  input  B0,
  input  E,
  input  X,
  output O
);

  wire and_1_out, and_2_out, and_3_out, and_4_out, and_5_out, and_6_out, and_7_out, and_8_out, and_9_out,
       and_10_out, and_11_out, and_12_out, and_13_out, and_14_out, and_15_out, and_16_out, and_17_out,
       and_18_out, and_19_out, not_1_out, not_2_out, not_3_out, not_4_out, not_5_out, not_6_out, not_7_out,
       not_8_out;

  not not_1 (not_1_out, B5);
  not not_2 (not_2_out, B4);
  not not_3 (not_3_out, B3);
  not not_4 (not_4_out, B2);
  not not_5 (not_5_out, B1);
  not not_6 (not_6_out, B0);
  not not_7 (not_7_out, E);
  not not_8 (not_8_out, X);
  and and_1 (and_1_out, not_1_out, not_2_out, not_3_out, B1, not_6_out, X);
  and and_2 (and_2_out, not_2_out, not_3_out, not_4_out, B1, X);
  and and_3 (and_3_out, not_4_out, B1, B0, E);
  and and_4 (and_4_out, not_1_out, not_2_out, not_3_out, B2, not_6_out);
  and and_5 (and_5_out, not_1_out, not_2_out, not_3_out, B2, not_7_out, not_8_out);
  and and_6 (and_6_out, B2, not_5_out, not_8_out);
  and and_7 (and_7_out, not_1_out, not_3_out, B2, B1, not_6_out, E);
  and and_8 (and_8_out, B3, not_4_out, not_5_out, not_6_out, X);
  and and_9 (and_9_out, B3, not_4_out, B1, B0);
  and and_10 (and_10_out, B3, B2, not_5_out, B0);
  and and_11 (and_11_out, B4, not_4_out, not_5_out, not_6_out, X);
  and and_12 (and_12_out, B4, not_4_out, B1, B0);
  and and_13 (and_13_out, B4, B2, not_5_out, B0);
  and and_14 (and_14_out, B4, B3, B1, not_6_out);
  and and_15 (and_15_out, B5, not_3_out, not_4_out, not_6_out, X);
  and and_16 (and_16_out, B5, not_3_out, not_4_out, B1);
  and and_17 (and_17_out, B5, not_3_out, B1, not_6_out, not_7_out);
  and and_18 (and_18_out, B5, B2, not_6_out, not_7_out, not_8_out);
  and and_19 (and_19_out, B5, B2, not_5_out, B0);
  or or_1 (O, and_1_out, and_2_out, and_3_out, and_4_out, and_5_out, and_6_out, and_7_out, and_8_out, and_9_out, and_10_out, and_11_out, and_12_out, and_13_out, and_14_out, and_15_out, and_16_out, and_17_out, and_18_out, and_19_out);
endmodule

module B1Prime (
  input  B5,
  input  B4,
  input  B3,
  input  B2,
  input  B1,
  input  B0,
  input  E,
  input  X,
  output O
);

  wire and_1_out, and_2_out, and_3_out, and_4_out, and_5_out, and_6_out, and_7_out, and_8_out, and_9_out,
       and_10_out, and_11_out, and_12_out, and_13_out, not_1_out, not_2_out, not_3_out, not_4_out, not_5_out,
       not_6_out, not_7_out;

  not not_1 (not_1_out, B5);
  not not_2 (not_2_out, B4);
  not not_3 (not_3_out, B3);
  not not_4 (not_4_out, B2);
  not not_5 (not_5_out, B1);
  not not_6 (not_6_out, B0);
  not not_7 (not_7_out, E);
  and and_1 (and_1_out, not_1_out, not_2_out, not_3_out, B0, X);
  and and_2 (and_2_out, not_5_out, B0, E);
  and and_3 (and_3_out, not_1_out, not_2_out, not_3_out, B1, not_6_out);
  and and_4 (and_4_out, not_1_out, not_2_out, not_3_out, B1, not_7_out);
  and and_5 (and_5_out, not_3_out, not_4_out, B1, not_6_out);
  and and_6 (and_6_out, not_3_out, B1, not_6_out, not_7_out);
  and and_7 (and_7_out, not_1_out, not_2_out, not_3_out, B1, X);
  and and_8 (and_8_out, not_1_out, not_2_out, not_3_out, B2, X);
  and and_9 (and_9_out, not_1_out, not_2_out, B3, not_5_out, X);
  and and_10 (and_10_out, B3, B2, not_5_out, B0);
  and and_11 (and_11_out, B3, B2, B1, not_6_out, E);
  and and_12 (and_12_out, B4, not_5_out, B0);
  and and_13 (and_13_out, B5, not_5_out, B0);
  or or_1 (O, and_1_out, and_2_out, and_3_out, and_4_out, and_5_out, and_6_out, and_7_out, and_8_out, and_9_out, and_10_out, and_11_out, and_12_out, and_13_out);
endmodule

module B0Prime (
  input  B5,
  input  B4,
  input  B3,
  input  B2,
  input  B1,
  input  B0,
  input  E,
  input  X,
  output O
);

  wire and_1_out, and_2_out, and_3_out, and_4_out, and_5_out, and_6_out, and_7_out, and_8_out, and_9_out,
       and_10_out, and_11_out, and_12_out, and_13_out, not_1_out, not_2_out, not_3_out, not_4_out, not_5_out,
       not_6_out, not_7_out, not_8_out;

  not not_1 (not_1_out, B5);
  not not_2 (not_2_out, B4);
  not not_3 (not_3_out, B3);
  not not_4 (not_4_out, B2);
  not not_5 (not_5_out, B1);
  not not_6 (not_6_out, B0);
  not not_7 (not_7_out, E);
  not not_8 (not_8_out, X);
  and and_1 (and_1_out, not_1_out, not_2_out, not_3_out, not_6_out, E);
  and and_2 (and_2_out, not_5_out, not_6_out, E, not_8_out);
  and and_3 (and_3_out, not_1_out, not_2_out, not_3_out, B0, not_7_out);
  and and_4 (and_4_out, not_1_out, not_2_out, not_4_out, not_5_out, B0, not_7_out);
  and and_5 (and_5_out, not_1_out, not_2_out, not_3_out, B0, X);
  and and_6 (and_6_out, not_1_out, not_2_out, not_3_out, B1, X);
  and and_7 (and_7_out, not_1_out, not_2_out, not_3_out, B2, X);
  and and_8 (and_8_out, not_1_out, not_2_out, B3, not_4_out, not_5_out, X);
  and and_9 (and_9_out, B3, B2, B1, not_6_out, not_7_out);
  and and_10 (and_10_out, B4, not_4_out, B1, not_6_out, E);
  and and_11 (and_11_out, B4, B2, B1, not_6_out, not_7_out);
  and and_12 (and_12_out, B5, not_4_out, B1, not_6_out, E);
  and and_13 (and_13_out, B5, B2, B1, not_6_out, not_7_out);
  or or_1 (O, and_1_out, and_2_out, and_3_out, and_4_out, and_5_out, and_6_out, and_7_out, and_8_out, and_9_out, and_10_out, and_11_out, and_12_out, and_13_out);
endmodule

module C3 (
  input  B5,
  input  B4,
  input  B3,
  input  B2,
  input  B1,
  input  B0,
  output O
);

  wire and_1_out, and_2_out, and_3_out, not_1_out, not_2_out, not_3_out;

  not not_1 (not_1_out, B4);
  not not_2 (not_2_out, B2);
  not not_3 (not_3_out, B1);
  and and_1 (and_1_out, not_1_out, B3, not_2_out, not_3_out);
  and and_2 (and_2_out, B5, B2, B1, B0);
  and and_3 (and_3_out, B5, B3);
  or or_1 (O, and_1_out, and_2_out, and_3_out);
endmodule

module C2 (
  input  B5,
  input  B4,
  input  B3,
  input  B2,
  input  B1,
  input  B0,
  output O
);

  wire and_1_out, and_2_out, and_3_out, and_4_out, and_5_out, and_6_out, not_1_out, not_2_out, not_3_out,
       not_4_out, not_5_out, not_6_out;

  not not_1 (not_1_out, B5);
  not not_2 (not_2_out, B4);
  not not_3 (not_3_out, B3);
  not not_4 (not_4_out, B2);
  not not_5 (not_5_out, B1);
  not not_6 (not_6_out, B0);
  and and_1 (and_1_out, not_1_out, not_2_out, not_3_out, B2);
  and and_2 (and_2_out, not_1_out, not_3_out, B2, B1, B0);
  and and_3 (and_3_out, B4, B3);
  and and_4 (and_4_out, B5, not_3_out, not_4_out);
  and and_5 (and_5_out, B5, not_3_out, not_6_out);
  and and_6 (and_6_out, B5, B2, not_5_out, B0);
  or or_1 (O, and_1_out, and_2_out, and_3_out, and_4_out, and_5_out, and_6_out);
endmodule

module C1 (
  input  B5,
  input  B4,
  input  B3,
  input  B2,
  input  B1,
  input  B0,
  output O
);

  wire and_1_out, and_2_out, and_3_out, and_4_out, and_5_out, and_6_out, and_7_out, and_8_out, and_9_out,
       not_1_out, not_2_out, not_3_out, not_4_out, not_5_out, not_6_out;

  not not_1 (not_1_out, B5);
  not not_2 (not_2_out, B4);
  not not_3 (not_3_out, B3);
  not not_4 (not_4_out, B2);
  not not_5 (not_5_out, B1);
  not not_6 (not_6_out, B0);
  and and_1 (and_1_out, not_1_out, not_2_out, not_3_out, B1);
  and and_2 (and_2_out, not_3_out, B1, not_6_out);
  and and_3 (and_3_out, B3, B2, B1, B0);
  and and_4 (and_4_out, B4, not_3_out, not_4_out);
  and and_5 (and_5_out, B4, not_3_out, not_5_out);
  and and_6 (and_6_out, B4, not_3_out, not_6_out);
  and and_7 (and_7_out, B5, not_3_out, not_4_out);
  and and_8 (and_8_out, B5, not_3_out, not_5_out);
  and and_9 (and_9_out, B5, not_3_out, not_6_out);
  or or_1 (O, and_1_out, and_2_out, and_3_out, and_4_out, and_5_out, and_6_out, and_7_out, and_8_out, and_9_out);
endmodule

module C0 (
  input  B5,
  input  B4,
  input  B3,
  input  B2,
  input  B1,
  input  B0,
  output O
);

  wire and_1_out, and_2_out, and_3_out, and_4_out, and_5_out, and_6_out, and_7_out, not_1_out, not_2_out,
       not_3_out, not_4_out, not_5_out, not_6_out;

  not not_1 (not_1_out, B5);
  not not_2 (not_2_out, B4);
  not not_3 (not_3_out, B3);
  not not_4 (not_4_out, B2);
  not not_5 (not_5_out, B1);
  not not_6 (not_6_out, B0);
  and and_1 (and_1_out, not_1_out, not_2_out, not_3_out, B0);
  and and_2 (and_2_out, not_1_out, not_2_out, not_5_out, B0);
  and and_3 (and_3_out, not_4_out, B1, B0);
  and and_4 (and_4_out, B2, not_5_out, B0);
  and and_5 (and_5_out, B3, B2, not_6_out);
  and and_6 (and_6_out, B4, B2, not_6_out);
  and and_7 (and_7_out, B5, B2, not_6_out);
  or or_1 (O, and_1_out, and_2_out, and_3_out, and_4_out, and_5_out, and_6_out, and_7_out);
endmodule

module Seg7 (
  input  in_1,
  input  in_2,
  input  in_3,
  input  in_4,
  output out_5,
  output out_6,
  output out_7,
  output out_8,
  output out_9,
  output out_10,
  output out_11
);

  wire and_1_out, and_2_out, and_3_out, and_4_out, and_5_out, and_6_out, and_7_out, and_8_out, and_9_out,
       and_10_out, and_11_out, and_12_out, and_13_out, and_14_out, and_15_out, and_16_out, and_17_out,
       and_18_out, and_19_out, and_20_out, and_21_out, and_22_out, and_23_out, and_24_out, and_25_out,
       and_26_out, not_1_out, not_2_out, not_3_out, not_4_out;

  not not_1 (not_1_out, in_4);
  not not_2 (not_2_out, in_3);
  not not_3 (not_3_out, in_2);
  not not_4 (not_4_out, in_1);
  and and_1 (and_1_out, not_1_out, in_2);
  and and_2 (and_2_out, not_1_out, in_3, in_1);
  and and_3 (and_3_out, in_4, not_2_out, not_3_out);
  and and_4 (and_4_out, not_2_out, not_3_out, not_4_out);
  and and_5 (and_5_out, not_1_out, not_2_out);
  and and_6 (and_6_out, not_2_out, not_3_out);
  and and_7 (and_7_out, not_1_out, in_2, in_1);
  and and_8 (and_8_out, not_1_out, not_3_out, not_4_out);
  and and_9 (and_9_out, not_1_out, in_3);
  and and_10 (and_10_out, not_2_out, not_3_out);
  and and_11 (and_11_out, not_1_out, in_1);
  and and_12 (and_12_out, not_1_out, not_2_out, in_2);
  and and_13 (and_13_out, not_1_out, in_2, not_4_out);
  and and_14 (and_14_out, in_4, not_2_out, not_3_out);
  and and_15 (and_15_out, not_2_out, not_3_out, not_4_out);
  and and_16 (and_16_out, not_1_out, in_3, not_3_out, in_1);
  and and_17 (and_17_out, not_1_out, in_2, not_4_out);
  and and_18 (and_18_out, not_2_out, not_3_out, not_4_out);
  and and_19 (and_19_out, not_1_out, in_3, not_3_out);
  and and_20 (and_20_out, not_2_out, not_3_out, not_4_out);
  and and_21 (and_21_out, in_4, not_2_out, not_3_out);
  and and_22 (and_22_out, not_1_out, in_3, not_4_out);
  and and_23 (and_23_out, not_1_out, not_2_out, in_2);
  and and_24 (and_24_out, not_1_out, in_3, not_3_out);
  and and_25 (and_25_out, not_1_out, in_2, not_4_out);
  and and_26 (and_26_out, in_4, not_2_out, not_3_out);
  or or_1 (out_8, and_12_out, and_13_out, and_14_out, and_15_out, and_16_out);
  or or_2 (out_9, and_17_out, and_18_out);
  or or_3 (out_10, and_19_out, and_20_out, and_21_out, and_22_out);
  or or_4 (out_11, and_23_out, and_24_out, and_25_out, and_26_out);
  or or_5 (out_5, and_1_out, and_2_out, and_3_out, and_4_out);
  or or_6 (out_6, and_5_out, and_6_out, and_7_out, and_8_out);
  or or_7 (out_7, and_9_out, and_10_out, and_11_out);
endmodule

module LESelector (
  input  Le1,
  input  Le0,
  output Red,
  output Yellow,
  output Green
);

  nor nor_1 (Green, Le1, Le0);
  and and_1 (Red, Le1, ~Le0);  // AND_Gate
  and and_2 (Yellow, Le0, ~Le1);  // AND_Gate
endmodule

module LXSelector (
  input  Lx1,
  input  Lx0,
  output Red,
  output Yellow,
  output Green
);

  and and_1 (Red, Lx1, ~Lx0);  // AND_Gate
  and and_2 (Yellow, Lx0, ~Lx1);  // AND_Gate
  nor nor_1 (Green, Lx1, Lx0);
endmodule
